# Fritzing sketch RF receiver schematics (saved by Fritzing 0.9.3b)
breadboards: 1

parts:
  Raspberry_Pi_1 = Raspberry Pi 3 [part_number=RPI-3-V1.2]
  U1 = RF-LINK_RX [part_number="RXB12 - SYN470R" package=rf-link_rx]
  R1 = Resistor [tolerance=±5% resistance=100k package=THT]
  R2 = Resistor [tolerance=±5% resistance=220k package=THT]

nets:
  GND: Raspberry_Pi_1.GND, U1.GND, R2.Pin_0
  N1: Raspberry_Pi_1.GPIO27, R1.Pin_0, R2.Pin_1
  5V: Raspberry_Pi_1.5V, U1.+5V
  N2: U1.DATA, R1.Pin_1
